// Logisim project bcd_multiplier_Amaey_24EC10057.circ as structural Verilog: 1 circuit, main circuit main
module main (
  input  [3:0] in_1
);

  wire ic_74374_1_p9, ic_74374_1_p11, ic_74374_1_p12, ic_74374_1_p13, ic_74374_1_p14, n7408_1_pin3,
       n7408_1_pin6, n7408_1_pin8, n7408_1_pin9, n7408_1_pin11, n7408_2_pin1, n7408_2_pin2, n7408_2_pin3,
       n7408_2_pin4, n7408_2_pin10, n7408_2_pin13, n7408_3_pin2, n7408_4_pin3, n7408_4_pin6, n7408_4_pin8,
       n7408_4_pin11, n7408_4_pin12, n7408_4_pin13, n7408_5_pin2, n7408_6_pin2, n7432_1_pin3, n7432_1_pin11,
       n7432_2_pin3, n7432_2_pin8, n7432_2_pin11, n7447_1_pin9, n7447_1_pin10, n7447_1_pin11, n7447_1_pin12,
       n7447_1_pin13, n7447_1_pin14, n7447_1_pin15, n7447_2_pin9, n7447_2_pin10, n7447_2_pin11,
       n7447_2_pin12, n7447_2_pin13, n7447_2_pin14, n7447_2_pin15, n74283_1_pin1, n74283_1_pin2,
       n74283_1_pin3, n74283_1_pin4, n74283_1_pin5, n74283_1_pin7, n74283_1_pin10, n74283_1_pin12,
       n74283_1_pin13, n74283_1_pin14, n74283_2_pin1, n74283_2_pin2, n74283_2_pin3, n74283_2_pin4,
       n74283_2_pin5, n74283_2_pin6, n74283_2_pin7, n74283_2_pin9, n74283_2_pin10, n74283_2_pin11,
       n74283_2_pin12, n74283_2_pin13, n74283_2_pin14, n74283_2_pin15, n74283_3_pin1, n74283_3_pin2,
       n74283_3_pin4, n74283_3_pin10, n74283_3_pin13, n74283_4_pin1, n74283_4_pin2, n74283_4_pin4,
       n74283_4_pin6, n74283_4_pin9, n74283_4_pin10, n74283_4_pin11, n74283_4_pin13, n74283_4_pin15,
       n74283_5_pin2, n74283_5_pin10, n74283_5_pin13, n74283_6_pin2, n74283_6_pin6, n74283_6_pin11,
       n74283_6_pin15, n74283_7_pin1, n74283_7_pin4, n74283_7_pin10, n74283_7_pin13;

  _74283 u_74283_1 (
    .pin1(n74283_1_pin1), .pin2(n74283_1_pin2), .pin3(n74283_1_pin3), .pin4(n74283_1_pin4),
    .pin5(n74283_1_pin5), .pin6(n74283_1_pin2), .pin7(n74283_1_pin7), .pin15(n74283_1_pin7),
    .pin14(n74283_1_pin14), .pin13(n74283_1_pin13), .pin12(n74283_1_pin12), .pin11(n74283_1_pin7),
    .pin10(n74283_1_pin10));  // open: pin9
  _7408 u_7408_1 (
    .pin1(n74283_1_pin14), .pin2(n74283_1_pin3), .pin3(n7408_1_pin3), .pin4(n74283_1_pin14),
    .pin5(n74283_1_pin5), .pin6(n7408_1_pin6), .pin13(n74283_1_pin1), .pin12(n74283_1_pin4),
    .pin11(n7408_1_pin11), .pin10(n74283_1_pin1), .pin9(n7408_1_pin9), .pin8(n7408_1_pin8));
  _74283 u_74283_2 (
    .pin1(n74283_2_pin1), .pin2(n74283_2_pin2), .pin3(n74283_2_pin3), .pin4(n74283_2_pin4),
    .pin5(n74283_2_pin5), .pin6(n74283_2_pin6), .pin7(n74283_2_pin7), .pin15(n74283_2_pin15),
    .pin14(n74283_2_pin14), .pin13(n74283_2_pin13), .pin12(n74283_2_pin12), .pin11(n74283_2_pin11),
    .pin10(n74283_2_pin10), .pin9(n74283_2_pin9));
  _7408 u_7408_2 (
    .pin1(n7408_2_pin1), .pin2(n7408_2_pin2), .pin3(n7408_2_pin3), .pin4(n7408_2_pin4), .pin5(n7408_2_pin2),
    .pin6(n74283_2_pin5), .pin13(n7408_2_pin13), .pin12(n7408_2_pin2), .pin11(n74283_2_pin3),
    .pin10(n7408_2_pin10), .pin9(n7408_2_pin2), .pin8(n74283_2_pin14));
  _74283 u_74283_3 (
    .pin1(n74283_3_pin1), .pin2(n74283_3_pin2), .pin3(n74283_1_pin4), .pin4(n74283_3_pin4),
    .pin5(n7408_1_pin9), .pin6(n74283_3_pin2), .pin7(n74283_1_pin7), .pin15(n74283_1_pin7),
    .pin14(n74283_1_pin1), .pin13(n74283_3_pin13), .pin12(n74283_1_pin13), .pin11(n74283_1_pin7),
    .pin10(n74283_3_pin10));  // open: pin9
  _7432 u_7432_1 (
    .pin1(n7408_1_pin3), .pin2(n7408_1_pin6), .pin3(n7432_1_pin3), .pin4(n74283_1_pin12),
    .pin5(n7432_1_pin3), .pin6(n74283_1_pin2), .pin13(n7408_1_pin11), .pin12(n7408_1_pin8),
    .pin11(n7432_1_pin11), .pin10(n74283_1_pin13), .pin9(n7432_1_pin11), .pin8(n74283_3_pin2));
  _7408 u_7408_3 (
    .pin1(n7408_2_pin1), .pin2(n7408_3_pin2), .pin3(n74283_2_pin6), .pin4(n7408_2_pin4), .pin5(n7408_3_pin2),
    .pin6(n74283_2_pin2), .pin13(n7408_2_pin13), .pin12(n7408_3_pin2), .pin11(n74283_2_pin15),
    .pin10(n7408_2_pin10), .pin9(n7408_3_pin2), .pin8(n74283_2_pin11));
  _74283 u_74283_4 (
    .pin1(n74283_4_pin1), .pin2(n74283_4_pin2), .pin3(n74283_2_pin13), .pin4(n74283_4_pin4),
    .pin5(n74283_2_pin1), .pin6(n74283_4_pin6), .pin7(n74283_2_pin7), .pin15(n74283_4_pin15),
    .pin14(n74283_2_pin10), .pin13(n74283_4_pin13), .pin12(n74283_2_pin9), .pin11(n74283_4_pin11),
    .pin10(n74283_4_pin10), .pin9(n74283_4_pin9));
  _7408 u_7408_4 (
    .pin1(n74283_3_pin1), .pin2(n74283_3_pin4), .pin3(n7408_4_pin3), .pin4(n74283_3_pin1),
    .pin5(n74283_4_pin4), .pin6(n7408_4_pin6), .pin13(n7408_4_pin13), .pin12(n7408_4_pin12),
    .pin11(n7408_4_pin11), .pin10(n7408_4_pin13), .pin9(n74283_2_pin4), .pin8(n7408_4_pin8));
  _7408 u_7408_5 (
    .pin1(n7408_2_pin1), .pin2(n7408_5_pin2), .pin3(n74283_4_pin6), .pin4(n7408_2_pin4), .pin5(n7408_5_pin2),
    .pin6(n74283_4_pin2), .pin13(n7408_2_pin13), .pin12(n7408_5_pin2), .pin11(n74283_4_pin15),
    .pin10(n7408_2_pin10), .pin9(n7408_5_pin2), .pin8(n74283_4_pin11));
  _74283 u_74283_5 (
    .pin1(n7408_4_pin13), .pin2(n74283_5_pin2), .pin3(n74283_3_pin4), .pin4(n7408_4_pin12),
    .pin5(n74283_4_pin4), .pin6(n74283_5_pin2), .pin7(n74283_1_pin7), .pin15(n74283_1_pin7),
    .pin14(n74283_3_pin1), .pin13(n74283_5_pin13), .pin12(n74283_3_pin13), .pin11(n74283_1_pin7),
    .pin10(n74283_5_pin10));  // open: pin9
  _74283 u_74283_6 (
    .pin1(n74283_1_pin5), .pin2(n74283_6_pin2), .pin3(n74283_4_pin13), .pin4(n7408_1_pin9),
    .pin5(n74283_4_pin1), .pin6(n74283_6_pin6), .pin7(n74283_2_pin7), .pin15(n74283_6_pin15),
    .pin14(n74283_4_pin10), .pin13(n74283_1_pin3), .pin12(n74283_4_pin9), .pin11(n74283_6_pin11),
    .pin10(n74283_1_pin14), .pin9(n74283_1_pin12));
  _7432 u_7432_2 (
    .pin1(n7408_4_pin3), .pin2(n7408_4_pin6), .pin3(n7432_2_pin3), .pin4(n74283_3_pin13),
    .pin5(n7432_2_pin3), .pin6(n74283_5_pin2), .pin13(n7408_4_pin11), .pin12(n7408_4_pin8),
    .pin11(n7432_2_pin11), .pin10(n74283_5_pin13), .pin9(n7432_2_pin11), .pin8(n7432_2_pin8));
  _7408 u_7408_6 (
    .pin1(n7408_2_pin1), .pin2(n7408_6_pin2), .pin3(n74283_6_pin6), .pin4(n7408_2_pin4), .pin5(n7408_6_pin2),
    .pin6(n74283_6_pin2), .pin13(n7408_2_pin13), .pin12(n7408_6_pin2), .pin11(n74283_6_pin15),
    .pin10(n7408_2_pin10), .pin9(n7408_6_pin2), .pin8(n74283_6_pin11));
  _74283 u_74283_7 (
    .pin1(n74283_7_pin1), .pin2(n7432_2_pin8), .pin3(n7408_4_pin12), .pin4(n74283_7_pin4),
    .pin5(n74283_2_pin4), .pin6(n7432_2_pin8), .pin7(n74283_1_pin7), .pin15(n74283_1_pin7),
    .pin14(n7408_4_pin13), .pin13(n74283_7_pin13), .pin12(n74283_5_pin13), .pin11(n74283_1_pin7),
    .pin10(n74283_7_pin10));  // open: pin9
  _7447 u_7447_1 (
    .pin1(n74283_5_pin10), .pin2(n74283_3_pin10), .pin6(n74283_1_pin10), .pin7(n74283_7_pin10),
    .pin15(n7447_1_pin15), .pin14(n7447_1_pin14), .pin13(n7447_1_pin13), .pin12(n7447_1_pin12),
    .pin11(n7447_1_pin11), .pin10(n7447_1_pin10), .pin9(n7447_1_pin9));  // open: pin3, pin4, pin5
  _7_Segment_Display u_7_segment_display_1 (
    .g(n7447_1_pin14), .f(n7447_1_pin15), .a(n7447_1_pin13), .b(n7447_1_pin12), .e(n7447_1_pin9),
    .d(n7447_1_pin10), .c(n7447_1_pin11));  // open: dp
  _7_Segment_Display u_7_segment_display_2 (
    .g(n7447_2_pin14), .f(n7447_2_pin15), .a(n7447_2_pin13), .b(n7447_2_pin12), .e(n7447_2_pin9),
    .d(n7447_2_pin10), .c(n7447_2_pin11));  // open: dp
  _7447 u_7447_2 (
    .pin1(n74283_7_pin4), .pin2(n74283_7_pin1), .pin6(n74283_7_pin13), .pin7(n7408_2_pin3),
    .pin15(n7447_2_pin15), .pin14(n7447_2_pin14), .pin13(n7447_2_pin13), .pin12(n7447_2_pin12),
    .pin11(n7447_2_pin11), .pin10(n7447_2_pin10), .pin9(n7447_2_pin9));  // open: pin3, pin4, pin5
  // IC_74374 ic_74374_1: pin names not known; wires that end beside it: in_1[0], in_1[1], in_1[2], in_1[3], n7408_2_pin2, n7408_3_pin2, n7408_5_pin2, n7408_6_pin2, ic_74374_1_p9, 1'b0, ic_74374_1_p11, ic_74374_1_p12, ic_74374_1_p13, ic_74374_1_p14
  Hex_Digit_Display hex_digit_display_1 (.value(in_1));  // open: dp
  // IC_74173 ic_74173_1: pin names not known; wires that end beside it: ic_74374_1_p11, ic_74374_1_p12, ic_74374_1_p13, ic_74374_1_p14, ic_74374_1_p9, 1'b0, 1'b0, 1'b0, 1'b0, 1'b0, n7408_2_pin1, n7408_2_pin4, n7408_2_pin13, n7408_2_pin10
  Clock clock_1 (.out(ic_74374_1_p9));
  // also tied to GND on the sheet: {n74283_2_pin12, n74283_2_pin7, n74283_1_pin7}
endmodule
